// Logisim project Atividades de exercicio.circ as structural Verilog
module atv1 (
  input  in_1,
  input  A,
  input  in_3,
  input  B,
  input  C,
  input  in_6,
  input  A_2,
  input  X,
  input  B_2,
  input  Y,
  input  C_2,
  input  W,
  input  D,
  output out_14,
  output out_15,
  output out_16,
  output out_17
);

  wire and_1_out, and_2_out, and_4_out, and_5_out, and_6_out, not_1_out, not_2_out, not_3_out, not_4_out,
       not_5_out, not_6_out, or_1_out, or_2_out, or_4_out;

  not not_1 (not_1_out, in_3);
  or or_1 (or_1_out, in_1, in_3);
  or or_2 (or_2_out, not_1_out, in_6);
  not not_2 (not_2_out, C_2);
  and and_1 (and_1_out, C_2, D);
  and and_2 (and_2_out, A_2, B_2);
  not not_3 (not_3_out, and_1_out);
  and and_3 (out_14, or_1_out, or_2_out);
  or or_3 (out_17, and_2_out, not_2_out, not_3_out);
  not not_4 (not_4_out, Y);
  not not_5 (not_5_out, A);
  or or_4 (or_4_out, not_4_out, W);
  and and_4 (and_4_out, A, C);
  and and_5 (and_5_out, not_5_out, B, C);
  not not_6 (not_6_out, and_6_out);
  and and_6 (and_6_out, B, C);
  and and_7 (out_16, X, or_4_out);
  or or_5 (out_15, and_4_out, and_5_out, not_6_out);

  // Notes on the sheet:
  //   Atividade 1
  //   Atividade 3
  //   Atividade 2
  //   Atividade 4
endmodule
